// Logisim project 8bit_ALU.circ as structural Verilog: 1 circuit, main circuit main
module main (
  input  subtract,
  input  a0,
  input  b0,
  input  a1,
  input  b1,
  input  a2,
  input  b2,
  input  a3,
  input  b3,
  input  a4,
  input  b4,
  input  a5,
  input  b5,
  input  a6,
  input  b6,
  input  a7,
  input  b7,
  output ADDSUB0,
  output XOR0,
  output NOT0,
  output AND0,
  output ADDSUB1,
  output XOR1,
  output NOT1,
  output AND1,
  output ADDSUB2,
  output XOR2,
  output NOT2,
  output AND2,
  output ADDSUB3,
  output XOR3,
  output NOT3,
  output AND3,
  output ADDSUB4,
  output XOR4,
  output NOT4,
  output AND4,
  output ADDSUB5,
  output XOR5,
  output NOT5,
  output AND5,
  output ADDSUB6,
  output XOR6,
  output NOT6,
  output AND6,
  output ADDSUB7,
  output XOR7,
  output NOT7,
  output carry,
  output AND7
);

  wire and_9_out, and_10_out, and_11_out, and_12_out, and_13_out, and_14_out, and_15_out, and_16_out,
       or_1_out, or_2_out, or_3_out, or_4_out, or_5_out, or_6_out, or_7_out;

  xor xor_1 (NOT0, b0, subtract);
  xor xor_2 (NOT1, b1, subtract);
  xor xor_3 (NOT2, b2, subtract);
  xor xor_4 (NOT3, b3, subtract);
  xor xor_5 (NOT4, b4, subtract);
  xor xor_6 (NOT5, b5, subtract);
  xor xor_7 (NOT6, b6, subtract);
  xor xor_8 (NOT7, b7, subtract);
  xor xor_9 (XOR0, a0, NOT0);
  and and_1 (AND0, a0, NOT0);
  xor xor_10 (XOR1, a1, NOT1);
  and and_2 (AND1, a1, NOT1);
  xor xor_11 (XOR2, a2, NOT2);
  and and_3 (AND2, a2, NOT2);
  xor xor_12 (XOR3, a3, NOT3);
  and and_4 (AND3, a3, NOT3);
  xor xor_13 (XOR4, a4, NOT4);
  and and_5 (AND4, a4, NOT4);
  xor xor_14 (XOR5, a5, NOT5);
  and and_6 (AND5, a5, NOT5);
  xor xor_15 (XOR6, a6, NOT6);
  and and_7 (AND6, a6, NOT6);
  xor xor_16 (XOR7, a7, NOT7);
  and and_8 (AND7, a7, NOT7);
  xor xor_17 (ADDSUB0, XOR0, subtract);
  and and_9 (and_9_out, XOR0, subtract);
  xor xor_18 (ADDSUB1, XOR1, or_1_out);
  and and_10 (and_10_out, XOR1, or_1_out);
  xor xor_19 (ADDSUB2, XOR2, or_2_out);
  and and_11 (and_11_out, XOR2, or_2_out);
  xor xor_20 (ADDSUB3, XOR3, or_3_out);
  and and_12 (and_12_out, XOR3, or_3_out);
  xor xor_21 (ADDSUB4, XOR4, or_4_out);
  and and_13 (and_13_out, XOR4, or_4_out);
  xor xor_22 (ADDSUB5, XOR5, or_5_out);
  and and_14 (and_14_out, XOR5, or_5_out);
  xor xor_23 (ADDSUB6, XOR6, or_6_out);
  and and_15 (and_15_out, XOR6, or_6_out);
  xor xor_24 (ADDSUB7, XOR7, or_7_out);
  and and_16 (and_16_out, XOR7, or_7_out);
  or or_1 (or_1_out, and_9_out, AND0);
  or or_2 (or_2_out, and_10_out, AND1);
  or or_3 (or_3_out, and_11_out, AND2);
  or or_4 (or_4_out, and_12_out, AND3);
  or or_5 (or_5_out, and_13_out, AND4);
  or or_6 (or_6_out, and_14_out, AND5);
  or or_7 (or_7_out, and_15_out, AND6);
  or or_8 (carry, and_16_out, AND7);
endmodule
