// Logisim project carry_lookahead_adder.circ as structural Verilog: 1 circuit, main circuit main
module main (
  input  a,
  input  b,
  input  carry_in,
  output sum,
  output carry_propagator,
  output carry_generator
);

  xor xor_1 (carry_propagator, a, b);
  and and_1 (carry_generator, a, b);
  xor xor_2 (sum, carry_propagator, carry_in);
endmodule
